# Fritzing sketch schematic_v0.1 (saved by Fritzing 0.9.10b)
perfboards: 2

parts:
  Part1 = Arduino Mega ADK (Rev3)
  Q1 = Basic FET N-Channel [package="D2Pak [SMD]"]  # not connected
  Q2 = Basic FET N-Channel [package="D2Pak [SMD]"]  # not connected
  Q3 = Basic FET N-Channel [package="D2Pak [SMD]"]  # not connected
  Q4 = Basic FET N-Channel [package="D2Pak [SMD]"]  # not connected
  J1 = Camdenboss CTB0158-12 [part_number=CTB0158-12 package=THT]
  M1 = RioRand LM2596
  IC1 = MICROCONTROLLER [package=dil28-3-zif_socket]  # not connected
  J2 = Camdenboss CTB0158-2 [part_number=CTB0158-2 package=THT]  # not connected
  J3 = Camdenboss CTB0158-6 [part_number=CTB0158-6 package=THT]  # not connected
  J4 = Camdenboss CTB0158-2 [part_number=CTB0158-2 package=THT]  # not connected
  J5 = Camdenboss CTB0158-2 [part_number=CTB0158-2 package=THT]  # not connected
  J6 = Camdenboss CTB0158-2 [part_number=CTB0158-2 package=THT]  # not connected
  J7 = Camdenboss CTB0158-2 [part_number=CTB0158-2 package=THT]  # not connected
  J8 = Camdenboss CTB0158-2 [part_number=CTB0158-2 package=THT]  # not connected
  J9 = Camdenboss CTB0158-6 [part_number=CTB0158-6 package=THT]  # not connected
  LED1 = LEDs [package=led10mm]  # not connected
  M2 = DC Motor [voltage_(max)=6V voltage_(min)=3V]  # not connected
  LED2 = LEDs [package=led10mm]  # not connected
  M3 = DC Motor [voltage_(max)=6V voltage_(min)=3V]  # not connected
  LED3 = LEDs [package=led10mm]  # not connected
  M4 = DC Motor [voltage_(max)=6V voltage_(min)=3V]  # not connected
  LED4 = LEDs [package=led10mm]  # not connected
  M5 = DC Motor [voltage_(max)=6V voltage_(min)=3V]  # not connected
  J22 = Camdenboss CTB0158-6 [part_number=CTB0158-6 package=THT]  # not connected
  J24 = Camdenboss CTB0158-6 [part_number=CTB0158-6 package=THT]
  J25 = Camdenboss CTB0158-6 [part_number=CTB0158-6 package=THT]
  J26 = Camdenboss CTB0158-6 [part_number=CTB0158-6 package=THT]
  J27 = Camdenboss CTB0158-6 [part_number=CTB0158-6 package=THT]
  J23 = Camdenboss CTB0158-7 [part_number=CTB0158-7 package=THT]
  J28 = Camdenboss CTB0158-12 [part_number=CTB0158-12 package=THT]  # not connected
  J19 = Camdenboss CTB0158-5 [part_number=CTB0158-5 package=THT]
  J29 = Camdenboss CTB0158-5 [part_number=CTB0158-5 package=THT]
  J21 = Camdenboss CTB0158-5 [part_number=CTB0158-5 package=THT]
  J30 = Camdenboss CTB0158-5 [part_number=CTB0158-5 package=THT]
  J31 = Camdenboss CTB0158-5 [part_number=CTB0158-5 package=THT]
  J32 = Camdenboss CTB0158-5 [part_number=CTB0158-5 package=THT]
  J33 = Camdenboss CTB0158-5 [part_number=CTB0158-5 package=THT]
  J34 = Camdenboss CTB0158-5 [part_number=CTB0158-5 package=THT]
  J35 = Camdenboss CTB0158-5 [part_number=CTB0158-5 package=THT]
  J36 = Camdenboss CTB0158-5 [part_number=CTB0158-5 package=THT]
  J37 = Camdenboss CTB0158-5 [part_number=CTB0158-5 package=THT]
  J38 = Camdenboss CTB0158-5 [part_number=CTB0158-5 package=THT]
  J39 = female pin header, 14 pins [form="♀ (female)"]
  J40 = female pin header, 14 pins [form="♀ (female)"]

nets:
  N1: Part1.5V, J23.pin2
  N2: J1.pin1, J39.pin1, J39.pin2, J39.pin3, J40.pin5
  N3: J1.pin2, M1.Pin_2, M1.Pin_4
  N4: J24.pin2, J32.pin5
  N5: J24.pin3, J31.pin5
  N6: J24.pin4, J29.pin5
  N7: J24.pin5, J19.pin5
  N8: J25.pin3, J38.pin5
  N9: J25.pin4, J37.pin5
  N10: J25.pin5, J35.pin5
  N11: J25.pin6, J34.pin5
  N12: J26.pin2, J38.pin4
  N13: J26.pin3, J37.pin4
  N14: J26.pin4, J35.pin4
  N15: J26.pin5, J34.pin4
  N16: J26.pin6, J23.pin6, J39.pin4, J40.pin6
  N17: J27.pin2, J32.terminal_4
  N18: J27.pin3, J31.terminal_4
  N19: J27.pin4, J29.terminal_4
  N20: J27.pin5, J19.terminal_4
  N21: J27.terminal_6, J23.terminal_7
  N22: J23.pin5, J21.pin5, J30.pin5, J33.pin5, J36.pin5
  N23: J21.pin4, J30.pin4, J33.pin4, J36.pin4

notes:
  + 12V
  + 5V
  encoder
  display
  -
  + 5v
  B
  A
  Din
  CS
  CLK
  - 0V (from 12V)
